# Fritzing sketch memecimetro (saved by Fritzing 0.9.3b)

parts:
  Part1 = Arduino Pro Mini (3.3V)
  R1 = Resistor [tolerance=±5% resistance=2.2k package="2010 [SMD]"]
  Nokia_5110_LCD_Module1 = Nokia 5110 LCD
  S1 = Momentary Switch [package=ksa_sealed_tac_switch]
  VCC1 = Battery block 9V
  Q1 = PNP-Transistor [part_number=3144 package="SOT-23 [SMD]"]

nets:
  N1: Part1.RAW, VCC1.+
  GND: Part1.GND, Nokia_5110_LCD_Module1.GND, S1.4, VCC1.-, Q1.0
  VCC: Part1.VCC, Nokia_5110_LCD_Module1.VCC, Nokia_5110_LCD_Module1.VCC_(out), Q1.2
  N2: Part1.A0, Q1.1
  N3: Part1.SCK, Nokia_5110_LCD_Module1.SCLK
  N4: Part1.MOSI, Nokia_5110_LCD_Module1.DN(MOSI)
  N5: Part1.D9, R1.Pin_0
  N6: Part1.D7, Nokia_5110_LCD_Module1.SCE
  N7: Part1.D6, Nokia_5110_LCD_Module1.RST
  N8: Part1.D5, Nokia_5110_LCD_Module1.D/C
  N9: Part1.D2, S1.3
  N10: R1.Pin_1, Nokia_5110_LCD_Module1.LED

custom parts:
  Nokia 5110 LCD: Nokia 5110 Graphic 84*48 LCD module such as the Sparkfun LCD-10168 or the clones from Ebay. There is example code for the Arduino available from the Sparkfun site in https://learn.sparkfun.com/tutorials/graphic-lcd-hookup-guide This is a 3.3V device, if you are running it from a 5V micro you need a 5V tolorant level translator such as the 74ahc367 to protect the signal imputs. Rafa G. did a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
